// Logisim project circuito_trabalhofinal.circ as structural Verilog: 1 circuit, main circuit main
module main (
  input  M1,
  input  M2,
  input  BA,
  input  \AÇ ,
  input  BC
);

  wire and_1_out, and_2_out, and_3_out, and_4_out, and_5_out, and_6_out, and_7_out, and_8_out, and_9_out,
       and_10_out, and_11_out, and_12_out, and_13_out, and_14_out, and_15_out, and_16_out, and_17_out,
       and_18_out, and_19_out, and_20_out, and_21_out, and_22_out, and_23_out, and_24_out, and_25_out,
       and_26_out, and_27_out, and_28_out, clock_1_out, clock_2_out, D1_q, D1_qn, D2_q, D3_q, D4_q, d_ff_1_q,
       d_ff_1_qn, not_1_out, not_2_out, not_3_out, not_4_out, not_5_out, not_6_out, not_7_out, not_8_out,
       not_9_out, not_10_out, not_11_out, not_12_out, not_13_out, not_14_out, not_15_out, not_16_out,
       not_17_out, not_18_out, not_19_out, not_20_out, not_21_out, not_22_out, not_23_out, not_24_out,
       not_25_out, not_26_out, or_1_out, or_2_out, or_3_out, or_4_out, or_5_out, or_6_out, or_7_out,
       or_8_out, or_9_out, or_10_out, or_11_out, or_12_out, or_13_out;

  not not_1 (not_1_out, BA);
  not not_2 (not_2_out, M1);
  not not_3 (not_3_out, M2);
  and and_1 (and_1_out, M2, not_4_out, D1_q);
  not not_4 (not_4_out, d_ff_1_q);
  and and_2 (and_2_out, M1, not_3_out, not_5_out);
  not not_5 (not_5_out, d_ff_1_q);
  and and_3 (and_3_out, M2, d_ff_1_q, not_6_out);
  not not_6 (not_6_out, D1_q);
  and and_4 (and_4_out, not_2_out, d_ff_1_q, not_7_out);
  not not_7 (not_7_out, D1_q);
  and and_5 (and_5_out, M1, d_ff_1_q, not_8_out);
  not not_8 (not_8_out, D1_q);
  not not_9 (not_9_out, d_ff_1_q);
  and and_6 (and_6_out, not_9_out, D1_q);
  not not_10 (not_10_out, D1_q);
  and and_7 (and_7_out, not_10_out, M2);
  not not_11 (not_11_out, BC);
  or or_1 (or_1_out, and_1_out, and_2_out, and_3_out, and_4_out);
  and and_8 (and_8_out, or_1_out, not_26_out);
  Clock clock_1 (.out(clock_1_out));
  or or_2 (or_2_out, and_5_out, and_6_out, and_7_out);
  and and_9 (and_9_out, or_2_out, not_26_out);
  not not_12 (not_12_out, D3_q);
  not not_13 (not_13_out, D2_q);
  not not_14 (not_14_out, D3_q);
  not not_15 (not_15_out, D4_q);
  not not_16 (not_16_out, D2_q);
  not not_17 (not_17_out, D4_q);
  not not_18 (not_18_out, D3_q);
  D_Flip_Flop d_ff_1 (.clk(clock_1_out), .D(and_8_out), .Q(d_ff_1_q), .Qn(d_ff_1_qn));  // open: preset, en, reset
  D_Flip_Flop D1 (.clk(clock_1_out), .D(and_9_out), .Q(D1_q), .Qn(D1_qn));  // open: preset, en, reset
  not not_19 (not_19_out, D4_q);
  not not_20 (not_20_out, D3_q);
  not not_21 (not_21_out, D2_q);
  not not_22 (not_22_out, D2_q);
  not not_23 (not_23_out, D3_q);
  not not_24 (not_24_out, D2_q);
  and and_10 (and_10_out, d_ff_1_qn, D1_q);
  and and_11 (and_11_out, and_10_out, not_26_out);
  and and_12 (and_12_out, not_19_out, not_20_out, not_21_out, and_25_out);
  and and_13 (and_13_out, BA, not_22_out, D3_q);
  and and_14 (and_14_out, not_12_out, not_13_out, D4_q, \AÇ );
  and and_15 (and_15_out, D3_q, D2_q, not_1_out);
  and and_16 (and_16_out, D2_q, not_14_out, not_15_out, not_11_out);
  and and_17 (and_17_out, not_16_out, D3_q);
  and and_18 (and_18_out, D2_q, not_17_out, not_18_out, BC);
  and and_19 (and_19_out, D3_q, not_1_out);
  and and_20 (and_20_out, D4_q, not_23_out, not_24_out);
  and and_21 (and_21_out, D3_q, D2_q, BA);
  and and_22 (and_22_out, d_ff_1_qn, D1_qn);
  or or_3 (or_3_out, and_11_out, and_25_out);
  or or_4 (or_4_out, and_12_out, and_13_out, and_14_out, and_15_out, and_16_out);
  Clock clock_2 (.out(clock_2_out));
  and and_23 (and_23_out, D1_qn, d_ff_1_q);
  or or_5 (or_5_out, and_22_out, not_25_out);
  buf or_6 (or_6_out, or_5_out);  // OR_Gate
  _7_Segment_Display u_7_segment_display_1 (
    .g(or_3_out), .f(or_6_out), .a(or_10_out), .b(or_11_out), .e(or_7_out), .d(or_8_out), .c(or_12_out));  // open: dp
  or or_7 (or_7_out, or_5_out, and_11_out);
  or or_8 (or_8_out, or_5_out, and_11_out, and_25_out);
  D_Flip_Flop D2 (.clk(clock_2_out), .D(or_4_out), .Q(D2_q));  // open: Qn, preset, en, reset
  or or_9 (or_9_out, and_17_out, and_18_out, and_19_out);
  and and_24 (and_24_out, d_ff_1_q, D1_q);
  and and_25 (and_25_out, and_24_out, not_26_out);
  not not_25 (not_25_out, not_26_out);
  or or_10 (or_10_out, and_25_out, and_11_out, or_5_out);
  or or_11 (or_11_out, and_25_out, and_11_out, and_26_out, or_5_out);
  or or_12 (or_12_out, and_25_out, and_27_out, or_5_out);
  D_Flip_Flop D3 (.clk(clock_2_out), .D(or_9_out), .Q(D3_q));  // open: Qn, preset, en, reset
  D_Flip_Flop D4 (.clk(clock_2_out), .D(or_13_out), .Q(D4_q));  // open: Qn, preset, en, reset
  or or_13 (or_13_out, and_20_out, and_21_out);
  and and_26 (and_26_out, and_23_out, not_26_out);
  and and_27 (and_27_out, and_23_out, not_26_out);
  LED led_1 (.in(and_25_out));
  not not_26 (not_26_out, and_28_out);
  LED led_2 (.in(and_28_out));
  and and_28 (and_28_out, D2_q, D4_q);
endmodule
